# Fritzing sketch bicigenerador (saved by Fritzing 0.8.3b)
circuit board: 7.23628cm x 5.69846cm
breadboards: 1

parts:
  Relay = RELAY [package=relay-g5v]
  D1 = Diode [package=diode-1n4001]
  Alternador = Screw terminal - 2 pins [package=THT]
  BC547 = NPN-Transistor [package="TO92 [THT]"]
  R1 = Resistor [tolerance=±5% resistance=1k package=THT]
  Arduino = Arduino Uno (Rev3)
  GP2Y = screw terminal, 3 pins
  reed = Screw terminal - 2 pins [package=THT]
  R2 = Resistor [tolerance=±5% resistance=10k package=THT]
  RF_-_TX = RF Transmitter [package=THT]
  R3 = Resistor [tolerance=±5% resistance=220 package=THT]
  R4 = Resistor [tolerance=±5% resistance=220 package=THT]
  R5 = Resistor [tolerance=±5% resistance=220 package=THT]
  LED1 = RGB LED (com. anode, rbg) [package="5 mm [THT]"]

nets:
  N1: Relay.1, Alternador.pin1
  N2: Relay.2, D1.C, BC547.E
  N3: Relay.3, Alternador.pin2
  N4: Relay.5, D1.A, Arduino.5V, GP2Y.pin2, reed.pin1, R2.Pin_1, RF_-_TX.pin1, LED1.common_anode
  N5: BC547.B, R1.Pin_0
  N6: BC547.C, Arduino.GND, GP2Y.pin1, RF_-_TX.pin3
  N7: R1.Pin_1, Arduino.D7
  N8: Arduino.A0, GP2Y.pin3
  N9: Arduino.D2, reed.pin2, R2.Pin_0
  N10: Arduino.D3_PWM, R3.Pin_0
  N11: Arduino.D4, RF_-_TX.pin2
  N12: Arduino.D5_PWM, R5.Pin_0
  N13: Arduino.D6_PWM, R4.Pin_0
  N14: R3.Pin_1, LED1.red_cathode
  N15: R4.Pin_1, LED1.blue_cathode
  N16: R5.Pin_1, LED1.green_cathode

notes:
  Antena
  -
  +
  Data
  R
  G
  B
  Bicigenerador
  Luz & Fuerza
  2013
  RF - RX
  antenna
  relay
  BC547
  reed
  LED
  alternador
  diode
  GP2Y
  10k
  220
  1k

custom parts:
  RELAY: HJR-3FF
  RF Transmitter: Transmitter for RWS 371 receiver
